// Logisim project Adder-Subtracter.circ as structural Verilog: 6 circuits, main circuit main
module Full_Adder (
  input  in_1,
  input  in_2,
  input  in_3,
  output out_4,
  output out_5
);

  wire and_1_out, and_2_out, xor_1_out;

  xor xor_1 (xor_1_out, in_2, in_3);
  and and_1 (and_1_out, in_2, in_3);
  xor xor_2 (out_4, in_1, xor_1_out);
  and and_2 (and_2_out, xor_1_out, in_1);
  or or_1 (out_5, and_2_out, and_1_out);
endmodule

module HALF_ADDER (
  input  in_1,
  input  in_2,
  output out_3,
  output out_4
);

  xor xor_1 (out_3, in_1, in_2);
  and and_1 (out_4, in_1, in_2);
endmodule

module complementer (
  input  in_1,
  input  in_2,
  output out_3
);

  xor xor_1 (out_3, in_1, in_2);
endmodule

module _4BIT_2_complementer (
  input  [3:0] in_1,
  input  in_2,
  output [3:0] out_3
);

  complementer complementer_1 (.in_1(in_1[0]), .in_2(in_2), .out_3(out_3[0]));
  complementer complementer_2 (.in_1(in_1[1]), .in_2(in_2), .out_3(out_3[1]));
  complementer complementer_3 (.in_1(in_1[2]), .in_2(in_2), .out_3(out_3[2]));
  complementer complementer_4 (.in_1(in_1[3]), .in_2(in_2), .out_3(out_3[3]));
endmodule

module _4BIT_ADDER (
  input  [3:0] in_1,
  input  [3:0] in_2,
  input  in_3,
  output [3:0] out_4,
  output out_5,
  output out_6
);

  wire full_adder_1_out_5, full_adder_2_out_5;
  wire [3:0] n4bit_2_complementer_1_out_3;

  _4BIT_2_complementer u_4bit_2_complementer_1 (.in_1(in_2), .in_2(in_3), .out_3(n4bit_2_complementer_1_out_3));
  Full_Adder full_adder_1 (
    .in_2(in_1[0]), .in_3(n4bit_2_complementer_1_out_3[0]), .in_1(in_3), .out_5(full_adder_1_out_5),
    .out_4(out_4[0]));
  Full_Adder full_adder_2 (
    .in_2(in_1[1]), .in_3(n4bit_2_complementer_1_out_3[1]), .in_1(full_adder_1_out_5),
    .out_5(full_adder_2_out_5), .out_4(out_4[1]));
  Full_Adder full_adder_3 (
    .in_2(in_1[2]), .in_3(n4bit_2_complementer_1_out_3[2]), .in_1(full_adder_2_out_5), .out_5(out_5),
    .out_4(out_4[2]));
  Full_Adder full_adder_4 (
    .in_2(in_1[3]), .in_3(n4bit_2_complementer_1_out_3[3]), .in_1(out_5), .out_5(out_6), .out_4(out_4[3]));
endmodule

module main (
  input  [3:0] in_1,
  input  [3:0] in_2,
  input  in_3,
  output out_4,
  output out_5,
  output out_6,
  output out_7
);

  wire decoder_1_out0, decoder_1_out1, decoder_1_out2, decoder_1_out3, decoder_1_out4, decoder_1_out5,
       decoder_1_out6, decoder_1_out7, decoder_1_out8, decoder_1_out9, decoder_1_out10, decoder_1_out11,
       decoder_1_out12, decoder_1_out13, decoder_1_out14, decoder_1_out15, n4bit_adder_1_out_5, or_1_out,
       or_2_out, or_3_out, or_4_out, or_5_out, or_6_out, or_7_out, or_8_out, or_9_out, or_10_out, or_11_out,
       or_12_out, or_13_out, or_14_out, or_15_out, or_16_out, or_17_out, or_18_out, or_19_out, or_20_out,
       or_21_out, or_22_out, or_23_out;
  wire [2:0] n4bit_adder_1_out_4;

  NotExactlyOne xnor_1 (
    .out(out_5), .in1(out_6), .in2(n4bit_adder_1_out_4[2]), .in3(n4bit_adder_1_out_4[1]),
    .in4(n4bit_adder_1_out_4[0]));
  _4BIT_ADDER u_4bit_adder_1 (
    .in_1(in_1), .in_2(in_2), .in_3(in_3), .out_6(out_7), .out_4({out_6, n4bit_adder_1_out_4}),
    .out_5(n4bit_adder_1_out_5));
  xor xor_1 (out_4, n4bit_adder_1_out_5, out_7);
  Decoder #(.select(4), .enable("false")) decoder_1 (
    .out0(decoder_1_out0), .out1(decoder_1_out1), .out2(decoder_1_out2), .out3(decoder_1_out3),
    .out4(decoder_1_out4), .out5(decoder_1_out5), .out6(decoder_1_out6), .out7(decoder_1_out7),
    .out8(decoder_1_out8), .out9(decoder_1_out9), .out10(decoder_1_out10), .out11(decoder_1_out11),
    .out12(decoder_1_out12), .out13(decoder_1_out13), .out14(decoder_1_out14), .out15(decoder_1_out15),
    .sel({out_6, n4bit_adder_1_out_4}));
  or or_1 (or_1_out, decoder_1_out15, decoder_1_out14, decoder_1_out13, decoder_1_out12, decoder_1_out11);
  or or_2 (or_2_out, or_1_out, decoder_1_out10, decoder_1_out9, decoder_1_out8);
  or or_3 (or_3_out, decoder_1_out1, decoder_1_out15);
  or or_4 (or_4_out, decoder_1_out2, decoder_1_out14);
  or or_5 (or_5_out, decoder_1_out3, decoder_1_out13);
  or or_6 (or_6_out, decoder_1_out4, decoder_1_out12);
  or or_7 (or_7_out, decoder_1_out5, decoder_1_out11);
  or or_8 (or_8_out, decoder_1_out6, decoder_1_out10);
  or or_9 (or_9_out, decoder_1_out7, decoder_1_out9);
  or or_10 (or_10_out, decoder_1_out0, or_3_out, or_4_out, or_5_out, or_6_out);
  or or_11 (or_11_out, decoder_1_out0, or_4_out, or_5_out, or_7_out, or_8_out);
  or or_12 (or_12_out, decoder_1_out0, or_6_out, or_7_out, or_8_out, or_9_out);
  or or_13 (or_13_out, or_4_out, or_5_out, or_6_out, or_7_out, or_8_out);
  or or_14 (or_14_out, decoder_1_out0, or_4_out, or_8_out, decoder_1_out8);
  or or_15 (or_15_out, decoder_1_out0, or_4_out, or_5_out, or_7_out);
  or or_16 (or_16_out, decoder_1_out0, or_3_out, or_5_out, or_6_out);
  or or_17 (or_17_out, or_10_out, or_9_out, decoder_1_out8);
  or or_18 (or_18_out, or_11_out, or_9_out, decoder_1_out8);
  or or_19 (or_19_out, or_12_out, decoder_1_out8);
  or or_20 (or_20_out, or_13_out, decoder_1_out8);
  buf or_21 (or_21_out, or_14_out);  // OR_Gate
  or or_22 (or_22_out, or_15_out, or_8_out, decoder_1_out8);
  or or_23 (or_23_out, or_16_out, or_7_out, or_8_out, or_9_out, decoder_1_out8);
  _7_Segment_Display u_7_segment_display_1 (.g(or_2_out));  // open: f, a, b, e, d, c, dp
  _7_Segment_Display u_7_segment_display_2 (
    .g(or_20_out), .f(or_19_out), .a(or_18_out), .b(or_17_out), .e(or_21_out), .d(or_22_out), .c(or_23_out));  // open: dp

  // Notes on the sheet:
  //   V Z S C
endmodule
